// Logisim project Lab1.circ as structural Verilog: 7 circuits, main circuit main
module main (
  input  in_1,
  input  in_2,
  input  A,
  input  in_4,
  input  S0,
  input  S1,
  input  S2,
  input  S3,
  input  A1,
  input  B1,
  input  S,
  input  [7:0] in_12,
  input  in_13,
  input  As,
  input  in_15,
  input  in_16,
  input  in_17,
  input  Bs,
  input  [7:0] in_19,
  input  Cin,
  input  in_21,
  input  in_22,
  input  in_23,
  input  AA,
  input  BB,
  input  CCin,
  output out_27,
  output out_28,
  output out_29,
  output [7:0] out_30,
  output Sum,
  output out_32,
  output out_33,
  output Cout,
  output out_35,
  output out_36,
  output SS,
  output CCout,
  output out_39
);

  wire and_1_out, and_2_out, and_3_out, and_4_out, and_5_out, and_6_out, and_7_out, and_8_out, and_9_out,
       and_10_out, and_11_out, and_12_out, and_13_out, and_14_out, and_15_out, and_16_out, and_17_out,
       and_18_out, and_19_out, and_20_out, and_21_out, and_22_out, and_23_out, and_24_out, and_25_out,
       and_26_out, and_27_out, and_28_out, and_29_out, and_30_out, and_31_out, and_32_out, not_1_out,
       not_2_out, not_3_out, not_4_out, not_5_out, or_1_out, or_2_out, or_8_out, or_11_out, or_12_out,
       or_13_out, or_14_out, or_15_out, or_16_out, or_17_out, or_18_out, or_19_out, or_20_out, or_21_out,
       or_22_out, or_23_out, or_24_out, or_25_out, xor_1_out, xor_2_out, xor_3_out, xor_7_out, xor_9_out,
       xor_10_out, xor_11_out, xor_12_out, xor_13_out, xor_14_out, xor_15_out, xor_16_out;

  and and_1 (and_1_out, AA, BB);
  and and_2 (and_2_out, xor_2_out, CCin);
  not not_1 (not_1_out, A);
  and and_3 (and_3_out, Bs, As);
  xor xor_1 (xor_1_out, in_21, in_22);
  and and_4 (and_4_out, in_22, in_21);
  or or_1 (or_1_out, in_22, in_21);
  xor xor_2 (xor_2_out, AA, BB);
  not not_2 (not_2_out, S);
  xor xor_3 (xor_3_out, As, Bs);
  or or_2 (or_2_out, Bs, As);
  xor xor_4 (out_35, xor_1_out, in_23);
  or or_3 (out_36, and_4_out, and_5_out);
  and and_5 (and_5_out, or_1_out, in_23);
  and and_6 (and_6_out, or_2_out, Cin);
  xor xor_5 (SS, xor_2_out, CCin);
  or or_4 (CCout, and_1_out, and_2_out);
  not not_3 (not_3_out, in_4);
  and and_7 (and_7_out, A1, not_2_out);
  and and_8 (and_8_out, B1, S);
  xor xor_6 (Sum, xor_3_out, Cin);
  or or_5 (Cout, and_3_out, and_6_out);
  and and_9 (and_9_out, A, not_3_out);
  and and_10 (and_10_out, not_1_out, in_4);
  or or_6 (out_29, and_7_out, and_8_out);
  or or_7 (out_27, and_9_out, and_10_out);
  and and_11 (and_11_out, in_16, in_15);
  or or_8 (or_8_out, in_16, in_15);
  xor xor_7 (xor_7_out, in_15, in_16);
  and and_12 (and_12_out, or_8_out, in_17);
  xor xor_8 (out_32, xor_7_out, in_17);
  or or_9 (out_33, and_11_out, and_12_out);
  not not_4 (not_4_out, in_1);
  not not_5 (not_5_out, in_2);
  and and_13 (and_13_out, S0, not_4_out, not_5_out);
  and and_14 (and_14_out, S1, not_4_out, in_2);
  and and_15 (and_15_out, S2, in_1, not_5_out);
  and and_16 (and_16_out, S3, in_1, in_2);
  or or_10 (out_28, and_13_out, and_14_out, and_15_out, and_16_out);
  and and_17 (and_17_out, in_19[0], in_12[0]);
  or or_11 (or_11_out, in_19[0], in_12[0]);
  and and_18 (and_18_out, in_19[1], in_12[1]);
  or or_12 (or_12_out, in_19[1], in_12[1]);
  and and_19 (and_19_out, in_19[3], in_12[3]);
  or or_13 (or_13_out, in_19[3], in_12[3]);
  xor xor_9 (xor_9_out, in_12[0], in_19[0]);
  and and_20 (and_20_out, or_11_out, in_13);
  xor xor_10 (xor_10_out, in_12[1], in_19[1]);
  and and_21 (and_21_out, or_12_out, or_19_out);
  xor xor_11 (xor_11_out, in_12[2], in_19[2]);
  and and_22 (and_22_out, in_19[2], in_12[2]);
  or or_14 (or_14_out, in_19[2], in_12[2]);
  and and_23 (and_23_out, or_14_out, or_20_out);
  xor xor_12 (xor_12_out, in_12[3], in_19[3]);
  and and_24 (and_24_out, or_13_out, or_21_out);
  xor xor_13 (xor_13_out, in_12[4], in_19[4]);
  and and_25 (and_25_out, in_19[4], in_12[4]);
  or or_15 (or_15_out, in_19[4], in_12[4]);
  and and_26 (and_26_out, or_15_out, or_22_out);
  xor xor_14 (xor_14_out, in_12[5], in_19[5]);
  and and_27 (and_27_out, in_19[5], in_12[5]);
  or or_16 (or_16_out, in_19[5], in_12[5]);
  and and_28 (and_28_out, or_16_out, or_23_out);
  xor xor_15 (xor_15_out, in_12[6], in_19[6]);
  and and_29 (and_29_out, in_19[6], in_12[6]);
  or or_17 (or_17_out, in_19[6], in_12[6]);
  xor xor_16 (xor_16_out, in_12[7], in_19[7]);
  and and_30 (and_30_out, in_19[7], in_12[7]);
  or or_18 (or_18_out, in_19[7], in_12[7]);
  and and_31 (and_31_out, or_18_out, or_25_out);
  xor xor_17 (out_30[0], xor_9_out, in_13);
  or or_19 (or_19_out, and_17_out, and_20_out);
  xor xor_18 (out_30[1], xor_10_out, or_19_out);
  or or_20 (or_20_out, and_18_out, and_21_out);
  xor xor_19 (out_30[2], xor_11_out, or_20_out);
  or or_21 (or_21_out, and_22_out, and_23_out);
  xor xor_20 (out_30[3], xor_12_out, or_21_out);
  or or_22 (or_22_out, and_19_out, and_24_out);
  xor xor_21 (out_30[4], xor_13_out, or_22_out);
  or or_23 (or_23_out, and_25_out, and_26_out);
  xor xor_22 (out_30[5], xor_14_out, or_23_out);
  or or_24 (or_24_out, and_27_out, and_28_out);
  xor xor_23 (out_30[6], xor_15_out, or_24_out);
  or or_25 (or_25_out, and_29_out, and_32_out);
  and and_32 (and_32_out, or_17_out, or_24_out);
  xor xor_24 (out_30[7], xor_16_out, or_25_out);
  or or_26 (out_39, and_30_out, and_31_out);

  // Notes on the sheet:
  //   B
  //   CIRCUITO SUMADOR ADD1
  //   CIRCUITO XOR
  //   CIRCUITO MUX2
  //   A*¬B
  //   ¬A*B
  //   A*¬B + ¬A*B
  //   CIRCUITO MUX4
endmodule

module CXOR (
  input  A,
  input  B,
  output S
);

  wire and_1_out, and_2_out, not_1_out, not_2_out;

  not not_1 (not_1_out, A);
  not not_2 (not_2_out, B);
  and and_1 (and_1_out, A, not_2_out);
  and and_2 (and_2_out, not_1_out, B);
  or or_1 (S, and_1_out, and_2_out);

  // Notes on the sheet:
  //   CIRCUITO XOR
endmodule

module MUX2 (
  input  A,
  input  B,
  input  C,
  output S
);

  wire and_1_out, and_2_out, not_1_out;

  not not_1 (not_1_out, C);
  and and_1 (and_1_out, A, not_1_out);
  and and_2 (and_2_out, B, C);
  or or_1 (S, and_1_out, and_2_out);

  // Notes on the sheet:
  //   CIRCUITO MUX2
endmodule

module MUX4 (
  input  C0,
  input  C1,
  input  A,
  input  B,
  input  C,
  input  D,
  output S
);

  wire and_1_out, and_2_out, and_3_out, and_4_out, not_1_out, not_2_out;

  not not_1 (not_1_out, C0);
  not not_2 (not_2_out, C1);
  and and_1 (and_1_out, A, not_1_out, not_2_out);
  and and_2 (and_2_out, B, not_1_out, C1);
  and and_3 (and_3_out, C, C0, not_2_out);
  and and_4 (and_4_out, D, C0, C1);
  or or_1 (S, and_1_out, and_2_out, and_3_out, and_4_out);

  // Notes on the sheet:
  //   CIRCUITO MUX4
endmodule

module ADD1 (
  input  A,
  input  B,
  input  Cin,
  output S,
  output Cout
);

  wire and_1_out, and_2_out, cxor_1_s;

  and and_1 (and_1_out, A, B);
  and and_2 (and_2_out, cxor_1_s, Cin);
  CXOR cxor_1 (.A(A), .B(B), .S(cxor_1_s));
  or or_1 (Cout, and_1_out, and_2_out);
  CXOR cxor_2 (.A(cxor_1_s), .B(Cin), .S(S));

  // Notes on the sheet:
  //   CIRCUITO ADD1
endmodule

module ADD8 (
  input  Cin,
  input  [7:0] A,
  input  [7:0] B,
  output [7:0] S,
  output Cout
);

  wire add1_1_cout, add1_2_cout, add1_3_cout, add1_4_cout, add1_5_cout, add1_6_cout, add1_7_cout;

  ADD1 add1_1 (.A(A[0]), .B(B[0]), .Cin(Cin), .S(S[0]), .Cout(add1_1_cout));
  ADD1 add1_2 (.A(A[1]), .B(B[1]), .Cin(add1_1_cout), .S(S[1]), .Cout(add1_2_cout));
  ADD1 add1_3 (.A(A[2]), .B(B[2]), .Cin(add1_2_cout), .S(S[2]), .Cout(add1_3_cout));
  ADD1 add1_4 (.A(A[3]), .B(B[3]), .Cin(add1_3_cout), .S(S[3]), .Cout(add1_4_cout));
  ADD1 add1_5 (.A(A[4]), .B(B[4]), .Cin(add1_4_cout), .S(S[4]), .Cout(add1_5_cout));
  ADD1 add1_6 (.A(A[5]), .B(B[5]), .Cin(add1_5_cout), .S(S[5]), .Cout(add1_6_cout));
  ADD1 add1_7 (.A(A[6]), .B(B[6]), .Cin(add1_6_cout), .S(S[6]), .Cout(add1_7_cout));
  ADD1 add1_8 (.A(A[7]), .B(B[7]), .Cin(add1_7_cout), .S(S[7]), .Cout(Cout));

  // Notes on the sheet:
  //   CIRCUITO ADD8
endmodule

module ALU (
  input  [1:0] OP,
  input  [7:0] B,
  input  [7:0] A,
  input  in_4,
  input  in_5,
  output [7:0] R,
  output zero,
  output out_8,
  output out_9
);

  wire [7:0] add8_1_s, add8_2_s, and_1_out, not_1_out, or_1_out;

  assign not_1_out = ~B;  // NOT_Gate not_1, 8 bits wide
  assign and_1_out = A & B;  // AND_Gate and_1, 8 bits wide
  assign or_1_out = A | B;  // OR_Gate or_1, 8 bits wide
  ADD8 add8_1 (.Cin(in_4), .A(A), .B(B), .S(add8_1_s), .Cout(out_8));
  ADD8 add8_2 (.Cin(in_5), .A(A), .B(not_1_out), .S(add8_2_s), .Cout(out_9));
  Multiplexer #(.select(2), .width(8)) multiplexer_1 (
    .in0(and_1_out), .in1(or_1_out), .in2(add8_1_s), .in3(add8_2_s), .out(R), .sel(OP));
  nor nor_1 (zero, R[7], R[6], R[5], R[4], R[3], R[2], R[1], R[0]);

  // Notes on the sheet:
  //   CIRCUITO ALU
endmodule
