// Logisim project Lab2.circ as structural Verilog
module CXOR (
  input  A,
  input  B,
  output S
);

  wire and_1_out, and_2_out, not_1_out, not_2_out;

  not not_1 (not_1_out, A);
  not not_2 (not_2_out, B);
  and and_1 (and_1_out, A, not_2_out);
  and and_2 (and_2_out, not_1_out, B);
  or or_1 (S, and_1_out, and_2_out);

  // Notes on the sheet:
  //   CIRCUITO XOR
endmodule

module MUX2 (
  input  A,
  input  B,
  input  S,
  output R
);

  wire and_1_out, and_2_out, not_1_out;

  not not_1 (not_1_out, S);
  and and_1 (and_1_out, A, not_1_out);
  and and_2 (and_2_out, B, S);
  or or_1 (R, and_1_out, and_2_out);

  // Notes on the sheet:
  //   CIRCUITO MUX2
endmodule

module MUX4 (
  input  I0,
  input  I1,
  input  I2,
  input  I3,
  input  [1:0] S,
  output R
);

  wire mux2_1_r, mux2_2_r;

  MUX2 mux2_1 (.A(I0), .B(I1), .S(S[0]), .R(mux2_1_r));
  MUX2 mux2_2 (.A(I2), .B(I3), .S(S[0]), .R(mux2_2_r));
  MUX2 mux2_3 (.A(mux2_1_r), .B(mux2_2_r), .S(S[1]), .R(R));

  // Notes on the sheet:
  //   CIRCUITO MUX4
endmodule

module ADD1 (
  input  A,
  input  B,
  input  Cin,
  output S,
  output Cout
);

  wire and_1_out, and_2_out, cxor_1_s;

  and and_1 (and_1_out, A, B);
  and and_2 (and_2_out, cxor_1_s, Cin);
  CXOR cxor_1 (.A(A), .B(B), .S(cxor_1_s));
  or or_1 (Cout, and_1_out, and_2_out);
  CXOR cxor_2 (.A(cxor_1_s), .B(Cin), .S(S));

  // Notes on the sheet:
  //   CIRCUITO ADD1
endmodule

module ADD8 (
  input  Cin,
  input  [7:0] A,
  input  [7:0] B,
  output [7:0] S,
  output Cout
);

  wire add1_1_cout, add1_2_cout, add1_3_cout, add1_4_cout, add1_5_cout, add1_6_cout, add1_7_cout;

  ADD1 add1_1 (.A(A[0]), .B(B[0]), .Cin(Cin), .S(S[0]), .Cout(add1_1_cout));
  ADD1 add1_2 (.A(A[1]), .B(B[1]), .Cin(add1_1_cout), .S(S[1]), .Cout(add1_2_cout));
  ADD1 add1_3 (.A(A[2]), .B(B[2]), .Cin(add1_2_cout), .S(S[2]), .Cout(add1_3_cout));
  ADD1 add1_4 (.A(A[3]), .B(B[3]), .Cin(add1_3_cout), .S(S[3]), .Cout(add1_4_cout));
  ADD1 add1_5 (.A(A[4]), .B(B[4]), .Cin(add1_4_cout), .S(S[4]), .Cout(add1_5_cout));
  ADD1 add1_6 (.A(A[5]), .B(B[5]), .Cin(add1_5_cout), .S(S[5]), .Cout(add1_6_cout));
  ADD1 add1_7 (.A(A[6]), .B(B[6]), .Cin(add1_6_cout), .S(S[6]), .Cout(add1_7_cout));
  ADD1 add1_8 (.A(A[7]), .B(B[7]), .Cin(add1_7_cout), .S(S[7]), .Cout(Cout));

  // Notes on the sheet:
  //   CIRCUITO ADD8
endmodule

module ALU (
  input  [7:0] A,
  input  [7:0] B,
  input  [1:0] OP,
  input  in_4,
  output [7:0] R,
  output Zero,
  output out_7,
  output out_8
);

  wire [7:0] add8_1_s, add8_2_s, and_1_out, not_1_out, or_1_out;

  assign not_1_out = ~B;  // NOT_Gate not_1, 8 bits wide
  assign and_1_out = A & B;  // AND_Gate and_1, 8 bits wide
  assign or_1_out = A | B;  // OR_Gate or_1, 8 bits wide
  ADD8 add8_1 (.Cin(in_4), .A(A), .B(B), .S(add8_1_s), .Cout(out_7));
  ADD8 add8_2 (.Cin(1'b1), .A(A), .B(not_1_out), .S(add8_2_s), .Cout(out_8));
  MUX4de8bits mux4de8bits_1 (.A(and_1_out), .B(or_1_out), .C(add8_1_s), .D(add8_2_s), .C0(OP), .S(R));
  nor nor_1 (Zero, R[7], R[6], R[5], R[4], R[3], R[2], R[1], R[0]);

  // Notes on the sheet:
  //   CIRCUITO ALU
endmodule

module MUX4de8bits (
  input  [7:0] A,
  input  [7:0] B,
  input  [7:0] C,
  input  [7:0] D,
  input  [1:0] C0,
  output [7:0] S
);

  wire [7:0] mux2x8_1_s, mux2x8_2_s;

  MUX2x8 mux2x8_1 (.A(A), .B(B), .C0(C0[0]), .S(mux2x8_1_s));
  MUX2x8 mux2x8_2 (.A(C), .B(D), .C0(C0[0]), .S(mux2x8_2_s));
  MUX2x8 mux2x8_3 (.A(mux2x8_1_s), .B(mux2x8_2_s), .C0(C0[1]), .S(S));

  // Notes on the sheet:
  //   CIRCUITO MUX4 CON SALIDA DE 8 BITS
endmodule

module RSLatch (
  input  R,
  input  S,
  output Q,
  output Qbar
);

  nor nor_1 (Q, R, Qbar);
  nor nor_2 (Qbar, Q, S);

  // Notes on the sheet:
  //   Circuito RS Latch
endmodule

module DLatch (
  input  EN,
  input  D,
  input  RESET,
  output Q,
  output Qbar
);

  wire and_1_out, and_2_out, and_3_out, not_1_out, not_2_out, or_1_out;

  not not_1 (not_1_out, D);
  and and_1 (and_1_out, EN, not_1_out);
  and and_2 (and_2_out, EN, D);
  not not_2 (not_2_out, RESET);
  or or_1 (or_1_out, and_1_out, RESET);
  and and_3 (and_3_out, and_2_out, not_2_out);
  RSLatch rslatch_1 (.R(or_1_out), .S(and_3_out), .Q(Q), .Qbar(Qbar));

  // Notes on the sheet:
  //   Circuito Latch D
endmodule

module DFlipFlop (
  input  CLK,
  input  D,
  input  RESET,
  output Q,
  output Qbar
);

  wire dlatch_1_q, not_1_out;

  not not_1 (not_1_out, CLK);
  DLatch dlatch_1 (.EN(not_1_out), .D(D), .RESET(RESET), .Q(dlatch_1_q));  // open: Qbar
  DLatch dlatch_2 (.EN(CLK), .D(dlatch_1_q), .RESET(RESET), .Q(Q), .Qbar(Qbar));
endmodule

module FlipFlopEnabled (
  input  CLK,
  input  EN,
  input  D,
  input  RESET,
  output Q,
  output Qbar
);

  wire and_1_out;

  and and_1 (and_1_out, CLK, EN);
  DFlipFlop dflipflop_1 (.CLK(and_1_out), .D(D), .RESET(RESET), .Q(Q), .Qbar(Qbar));
endmodule

module LatchDLogisim (
  input  D,
  input  CLK,
  input  Qbar,
  input  RESET,
  output Q
);

  wire dlatch_1_q;

  DFlipFlop dflipflop_1 (.CLK(CLK), .D(D), .Q(Q));  // open: RESET, Qbar
  DLatch dlatch_1 (.EN(CLK), .D(D), .RESET(RESET), .Q(dlatch_1_q));  // open: Qbar
endmodule

module DFF_RISE_FALL (
  input  RESET,
  input  CLK,
  input  D,
  output Q_RISE,
  output Q_FALL
);

  wire not_1_out;

  not not_1 (not_1_out, CLK);
  DFlipFlop DFF_RISE (.CLK(CLK), .D(D), .RESET(RESET), .Q(Q_RISE));  // open: Qbar
  DFlipFlop DFF_FALL (.CLK(not_1_out), .D(D), .RESET(RESET), .Q(Q_FALL));  // open: Qbar
endmodule

module FF_D_J_JK (
  input  D,
  input  T,
  input  J,
  input  K,
  input  CKL,
  output Q_D,
  output Q_T,
  output Q_JK
);

  D_Flip_Flop FF_D (.D(D), .clk(CKL), .Q(Q_D));  // open: Qn, preset, reset
  T_Flip_Flop FF_T (.T(T), .clk(CKL), .Q(Q_T));  // open: Qn, reset, preset
  J_K_Flip_Flop FF_JK (.J(J), .K(K), .clk(CKL), .Q(Q_JK));  // open: Qn, preset, reset
endmodule

module CNT2_D (
  input  RESET,
  input  CLK,
  output [1:0] out_3
);

  wire cxor_1_s, dflipflop_2_qbar;

  CXOR cxor_1 (.A(out_3[1]), .B(out_3[0]), .S(cxor_1_s));
  DFlipFlop dflipflop_1 (.CLK(CLK), .D(cxor_1_s), .RESET(RESET), .Q(out_3[1]));  // open: Qbar
  DFlipFlop dflipflop_2 (.CLK(CLK), .D(dflipflop_2_qbar), .RESET(RESET), .Q(out_3[0]), .Qbar(dflipflop_2_qbar));
endmodule

module REG8 (
  input  CLEAR,
  input  CLK,
  input  [7:0] D,
  input  LOAD,
  input  RESET,
  output [7:0] Q
);

  wire not_1_out;
  wire [7:0] mux2x8_1_s, mux2x8_2_s;

  not not_1 (not_1_out, LOAD);
  MUX2x8 mux2x8_1 (.A(D), .B(Q), .C0(not_1_out), .S(mux2x8_1_s));
  MUX2x8 mux2x8_2 (.A(mux2x8_1_s), .B({8{1'b0}}), .C0(RESET), .S(mux2x8_2_s));
  FFDx8 ffdx8_1 (.CLEAR(CLEAR), .CLK(CLK), .D(mux2x8_2_s), .Q(Q));
endmodule

module MUX2x8 (
  input  [7:0] A,
  input  [7:0] B,
  input  C0,
  output [7:0] S
);

  MUX2 mux2_1 (.A(A[0]), .B(B[0]), .S(C0), .R(S[0]));
  MUX2 mux2_2 (.A(A[1]), .B(B[1]), .S(C0), .R(S[1]));
  MUX2 mux2_3 (.A(A[2]), .B(B[2]), .S(C0), .R(S[2]));
  MUX2 mux2_4 (.A(A[3]), .B(B[3]), .S(C0), .R(S[3]));
  MUX2 mux2_5 (.A(A[4]), .B(B[4]), .S(C0), .R(S[4]));
  MUX2 mux2_6 (.A(A[5]), .B(B[5]), .S(C0), .R(S[5]));
  MUX2 mux2_7 (.A(A[6]), .B(B[6]), .S(C0), .R(S[6]));
  MUX2 mux2_8 (.A(A[7]), .B(B[7]), .S(C0), .R(S[7]));
endmodule

module FFDx8 (
  input  CLEAR,
  input  CLK,
  input  [7:0] D,
  output [7:0] Q
);

  DFlipFlop dflipflop_1 (.CLK(CLK), .D(D[0]), .RESET(CLEAR), .Q(Q[0]));  // open: Qbar
  DFlipFlop dflipflop_2 (.CLK(CLK), .D(D[1]), .RESET(CLEAR), .Q(Q[1]));  // open: Qbar
  DFlipFlop dflipflop_3 (.CLK(CLK), .D(D[2]), .RESET(CLEAR), .Q(Q[2]));  // open: Qbar
  DFlipFlop dflipflop_4 (.CLK(CLK), .D(D[3]), .RESET(CLEAR), .Q(Q[3]));  // open: Qbar
  DFlipFlop dflipflop_5 (.CLK(CLK), .D(D[4]), .RESET(CLEAR), .Q(Q[4]));  // open: Qbar
  DFlipFlop dflipflop_6 (.CLK(CLK), .D(D[5]), .RESET(CLEAR), .Q(Q[5]));  // open: Qbar
  DFlipFlop dflipflop_7 (.CLK(CLK), .D(D[6]), .RESET(CLEAR), .Q(Q[6]));  // open: Qbar
  DFlipFlop dflipflop_8 (.CLK(CLK), .D(D[7]), .RESET(CLEAR), .Q(Q[7]));  // open: Qbar
endmodule

module CNT8 (
  input  CLEAR,
  input  CLK,
  input  RESET,
  input  ENABLE,
  output [7:0] Q
);

  wire [7:0] add8_1_s, mux2x8_1_s;

  ADD8 add8_1 (.Cin(1'b0), .A(Q), .B(8'h1), .S(add8_1_s));  // open: Cout
  MUX2x8 mux2x8_1 (.A(Q), .B(add8_1_s), .C0(ENABLE), .S(mux2x8_1_s));
  REG8 reg8_1 (.CLEAR(CLEAR), .CLK(CLK), .D(mux2x8_1_s), .LOAD(1'b1), .RESET(RESET), .Q(Q));
endmodule

module FSM101TEST (
  input  X,
  input  CLEAR,
  input  RESET,
  input  CKL,
  output out_5
);

  wire and_1_out, and_2_out, and_3_out, and_4_out, dflipflop_2_q, not_1_out, not_2_out, not_3_out, or_1_out;

  not not_1 (not_1_out, X);
  and and_1 (and_1_out, dflipflop_2_q, not_1_out);
  not not_2 (not_2_out, dflipflop_2_q);
  and and_2 (and_2_out, and_1_out, not_2_out, X);
  not not_3 (not_3_out, RESET);
  or or_1 (or_1_out, and_1_out, and_2_out);
  and and_3 (and_3_out, or_1_out, not_3_out);
  and and_4 (and_4_out, X, not_3_out);
  DFlipFlop dflipflop_1 (.CLK(CKL), .D(and_3_out), .RESET(CLEAR), .Q(and_1_out));  // open: Qbar
  DFlipFlop dflipflop_2 (.CLK(CKL), .D(and_4_out), .RESET(CLEAR), .Q(dflipflop_2_q));  // open: Qbar
  and and_5 (out_5, and_1_out, dflipflop_2_q);
endmodule

module NEXT_STATE101 (
  input  X,
  input  RESET,
  input  Q1,
  input  Q0,
  output D1,
  output D0
);

  wire and_1_out, and_2_out, or_1_out, Q0bar_out, RESETbar_out, Xbar_out;

  not Xbar (Xbar_out, X);
  not RESETbar (RESETbar_out, RESET);
  not Q0bar (Q0bar_out, Q0);
  and and_1 (and_1_out, Xbar_out, Q0);
  and and_2 (and_2_out, Q1, Q0bar_out, X);
  or or_1 (or_1_out, and_1_out, and_2_out);
  and and_3 (D1, or_1_out, RESETbar_out);
  and and_4 (D0, X, RESETbar_out);
endmodule

module MEMORY101 (
  input  D1,
  input  D0,
  input  CLK,
  input  CLEAR,
  output Q1,
  output Q0
);

  DFlipFlop dflipflop_1 (.CLK(CLK), .D(D1), .RESET(CLEAR), .Q(Q1));  // open: Qbar
  DFlipFlop dflipflop_2 (.CLK(CLK), .D(D0), .RESET(CLEAR), .Q(Q0));  // open: Qbar
endmodule

module FSM101 (
  input  X,
  input  RESET,
  input  CLK,
  input  CLEAR,
  output Z
);

  wire memory101_1_q0, memory101_1_q1, next_state101_1_d0, next_state101_1_d1;

  NEXT_STATE101 next_state101_1 (
    .X(X), .RESET(RESET), .Q1(memory101_1_q1), .Q0(memory101_1_q0), .D1(next_state101_1_d1),
    .D0(next_state101_1_d0));
  MEMORY101 memory101_1 (
    .D1(next_state101_1_d1), .D0(next_state101_1_d0), .CLK(CLK), .CLEAR(CLEAR), .Q1(memory101_1_q1),
    .Q0(memory101_1_q0));
  and and_1 (Z, memory101_1_q1, memory101_1_q0);
endmodule
