// Logisim project laborga2.circ as structural Verilog
module PuertaXOR (
  input  B,
  input  A,
  output Q
);

  wire and_1_out, and_2_out, not_1_out, not_2_out;

  not not_1 (not_1_out, B);
  not not_2 (not_2_out, A);
  and and_1 (and_1_out, not_2_out, B);
  and and_2 (and_2_out, not_1_out, A);
  or or_1 (Q, and_1_out, and_2_out);
endmodule

module MUX2 (
  input  A,
  input  S,
  input  B,
  output Q
);

  wire and_1_out, and_2_out, not_1_out;

  not not_1 (not_1_out, S);
  and and_1 (and_1_out, A, not_1_out);
  or or_1 (Q, and_1_out, and_2_out);
  and and_2 (and_2_out, S, B);
endmodule

module MUX4 (
  input  S0,
  input  S1,
  input  I3,
  input  I2,
  input  I1,
  input  I0,
  output Q
);

  wire and_1_out, and_2_out, and_3_out, and_4_out, not_1_out, not_2_out;

  not not_1 (not_1_out, S0);
  not not_2 (not_2_out, S1);
  and and_1 (and_1_out, S0, S1, I3);
  and and_2 (and_2_out, S0, not_2_out, I2);
  and and_3 (and_3_out, not_1_out, S1, I1);
  and and_4 (and_4_out, not_2_out, not_1_out, I0);
  or or_1 (Q, and_1_out, and_2_out, and_3_out, and_4_out);
endmodule

module ADD1 (
  input  A,
  input  B,
  input  CIN,
  output S,
  output COUT
);

  wire and_1_out, and_2_out, or_1_out, xor_1_out;

  xor xor_1 (xor_1_out, A, B);
  and and_1 (and_1_out, B, A);
  or or_1 (or_1_out, B, A);
  xor xor_2 (S, xor_1_out, CIN);
  and and_2 (and_2_out, or_1_out, CIN);
  or or_2 (COUT, and_1_out, and_2_out);
endmodule

module ADD8 (
  input  CIN,
  input  [7:0] A,
  input  [7:0] B,
  output [7:0] S,
  output COUT
);

  wire add1_1_cout, add1_2_cout, add1_3_cout, add1_5_cout, add1_6_cout, add1_7_cout, add1_9_cout;

  ADD1 add1_1 (.A(A[0]), .B(B[0]), .CIN(CIN), .S(S[0]), .COUT(add1_1_cout));
  ADD1 add1_2 (.A(A[1]), .B(B[1]), .CIN(add1_1_cout), .S(S[1]), .COUT(add1_2_cout));
  ADD1 add1_3 (.A(A[2]), .B(B[2]), .CIN(add1_2_cout), .S(S[2]), .COUT(add1_3_cout));
  ADD1 add1_4 (.A(A[2]), .B(B[2]), .CIN(add1_2_cout), .S(S[2]), .COUT(add1_3_cout));
  ADD1 add1_5 (.A(A[3]), .B(B[3]), .CIN(add1_3_cout), .S(S[3]), .COUT(add1_5_cout));
  ADD1 add1_6 (.A(A[4]), .B(B[4]), .CIN(add1_5_cout), .S(S[4]), .COUT(add1_6_cout));
  ADD1 add1_7 (.A(A[5]), .B(B[5]), .CIN(add1_6_cout), .S(S[5]), .COUT(add1_7_cout));
  ADD1 add1_8 (.A(A[5]), .B(B[5]), .CIN(add1_6_cout), .S(S[5]), .COUT(add1_7_cout));
  ADD1 add1_9 (.A(A[6]), .B(B[6]), .CIN(add1_7_cout), .S(S[6]), .COUT(add1_9_cout));
  ADD1 add1_10 (.A(A[7]), .B(B[7]), .CIN(add1_9_cout), .S(S[7]), .COUT(COUT));
  ADD1 add1_11 (.A(A[7]), .B(B[7]), .CIN(add1_9_cout), .S(S[7]), .COUT(COUT));
endmodule

module ANDBITaBIT (
  input  [7:0] A,
  input  [7:0] B,
  output [7:0] Q
);

  assign Q = A & B;  // AND_Gate and_1, 8 bits wide
endmodule

module ORBITaBIT (
  input  [7:0] A,
  input  [7:0] B,
  output [7:0] Q
);

  assign Q = A | B;  // OR_Gate or_1, 8 bits wide
endmodule

module ALU (
  input  [1:0] OP,
  input  [7:0] A,
  input  [7:0] B,
  input  in_4,
  input  in_5,
  output [7:0] R,
  output out_7,
  output zero,
  output out_9
);

  wire [7:0] add8_1_s, add8_2_s, andbitabit_1_q, not_1_out, orbitabit_1_q;
  wire [7:1] nor_1_out;

  assign not_1_out = ~B;  // NOT_Gate not_1, 8 bits wide
  ANDBITaBIT andbitabit_1 (.A(A), .B(B), .Q(andbitabit_1_q));
  ORBITaBIT orbitabit_1 (.A(A), .B(B), .Q(orbitabit_1_q));
  ADD8 add8_1 (.CIN(in_4), .A(A), .B(B), .S(add8_1_s), .COUT(out_7));
  ADD8 add8_2 (.CIN(in_5), .A(A), .B(not_1_out), .S(add8_2_s), .COUT(out_9));
  Multiplexer #(.select(2), .width(8)) multiplexer_1 (
    .in0(andbitabit_1_q), .in1(orbitabit_1_q), .in2(add8_1_s), .in3(add8_2_s), .out(R), .sel(OP));
  assign {nor_1_out, zero} = ~(R | R);  // NOR_Gate nor_1, 8 bits wide
  // Pins of 1 and 8 bits meet at {nor_1_out, zero}
endmodule
